# Fritzing sketch Untitled Sketch (saved by Fritzing 0.9.4)
circuit board: 8.46667cm x 5.64444cm

parts:
  U1 = 555 Timer [part_number=INA128 package="DIP8 [THT]"]
  Q1 = NPN-Transistor [package="TO92 [THT]"]
  R1 = Temperature Sensor (Thermistor) [thermistor_type=NTC package=THT]
  C2 = Ceramic Capacitor [capacitance=47µF voltage=5V package="100 mil [THT, multilayer]"]
  R3 = Resistor [tolerance=±5% resistance=220 package=THT]
  Компонент3 = Arduino Micro (Rev3)
  R4 = Resistor [tolerance=±5% resistance=220 package=THT]
  D1 = Rectifier Diode [part_number=1N4001 package="300 mil [THT]"]
  R2 = Resistor [tolerance=±5% resistance=10k package=THT]
  S1 = Reed switch [package=THT]
  S2 = Reed switch [package=THT]
  S3 = Reed switch [package=THT]

nets:
  N1: U1.Ground, C2.0
  N2: U1.Trigger, S3.pin_1
  N3: U1.Output, S2.pin_1
  N4: U1.Reset, Q1.E, Компонент3.GND, R2.Pin_0
  N5: U1.Control_Voltage, S1.pin_1
  N6: U1.Threshold, R4.Pin_1
  N7: U1.Discharge, R1.pin_0, R3.Pin_1, Компонент3.5V
  N8: U1.Vcc_Supply_Voltage, C2.1
  N9: Q1.B, R4.Pin_0
  N10: Q1.C, R3.Pin_0, D1.anode
  N11: R1.pin_1, Компонент3.A0, R2.Pin_1
  N12: Компонент3.A1, D1.cathode

notes:
  SENSORS
  Microcontoller
